// Logisim project Saguii.circ as structural Verilog: 9 circuits, main circuit main
module main (
);

  wire CI, CI_v, CLK, PcSource, r1, r1_v, reset, RS, RS_v, ula_5_comp, WM, WM_v, WR, WR_v;
  wire [1:0] multiplexer_2_out, multiplexer_3_out, multiplexer_4_out, multiplexer_5_out, multiplexer_6_out,
       separa_1_e_ra, separa_1_e_rb, v_ra, v_rb;
  wire [2:0] ula_ctrl, ula_ctrl_v;
  wire [3:0] separa_1_e_op, v_op;
  wire [7:0] adder_1_out, bd_1_da, br_pe0_1_da, br_pe0_1_db, br_pe1_1_da, br_pe1_1_db, br_pe2_1_da,
       br_pe2_1_db, br_pe3_1_da, br_pe3_1_db, db, e_imm, multiplexer_1_out, multiplexer_7_out,
       multiplexer_8_out, multiplexer_9_out, multiplexer_10_out, multiplexer_11_out, multiplexer_12_out,
       multiplexer_13_out, multiplexer_14_out, multiplexer_15_out, multiplexer_16_out, ram_1_dout,
       ram_2_dout, ram_3_dout, ram_4_dout, ram_5_dout, register_1_q, rom_1_data, ula_out, ula_out_p0,
       ula_out_p1, ula_out_p2, ula_out_p3, v_imm;

  Clock clock_1 (.out(CLK));
  Register register_1 (.D(multiplexer_1_out), .en(1'b1), .clk(CLK), .Q(register_1_q), .clr(reset));
  Button button_1 (.out(reset));
  ROM rom_1 (.addr(register_1_q), .data(rom_1_data));
  Adder adder_1 (.a(8'h1), .b(register_1_q), .out(adder_1_out));  // open: cin, cout
  Multiplexer #(.width(8)) multiplexer_1 (.in0(adder_1_out), .in1(db), .out(multiplexer_1_out), .sel(PcSource));
  Multiplexer #(.width(2)) multiplexer_2 (.in0(v_ra), .in1(2'b01), .out(multiplexer_2_out), .sel(r1_v));
  // Probe on multiplexer_12_out
  Multiplexer #(.width(2)) multiplexer_3 (.in0(v_ra), .in1(2'b01), .out(multiplexer_3_out), .sel(r1_v));
  // Probe on multiplexer_13_out
  // Probe on multiplexer_14_out
  Multiplexer #(.width(2)) multiplexer_4 (.in0(v_ra), .in1(2'b01), .out(multiplexer_4_out), .sel(r1_v));
  Multiplexer #(.width(2)) multiplexer_5 (.in0(v_ra), .in1(2'b01), .out(multiplexer_5_out), .sel(r1_v));
  // Probe on multiplexer_15_out
  separa separa_1 (
    .instr(rom_1_data), .v_op(v_op), .e_op(separa_1_e_op), .v_ra(v_ra), .e_ra(separa_1_e_ra), .v_rb(v_rb),
    .e_rb(separa_1_e_rb), .v_imm(v_imm), .e_imm(e_imm));
  Multiplexer #(.width(2)) multiplexer_6 (.in0(separa_1_e_ra), .in1(2'b01), .out(multiplexer_6_out), .sel(r1));
  // Probe on separa_1_e_rb
  // Probe on multiplexer_16_out
  // Probe on multiplexer_6_out
  UC uc_1 (
    .OPCODE(v_op), .comp(1'b0), .WM(WM_v), .RS(RS_v), .r1(r1_v), .CI(CI_v), .WR(WR_v), .ula_ctrl(ula_ctrl_v));  // open: pc_s
  BR_pe0 br_pe0_1 (
    .CLK(CLK), .WD(multiplexer_12_out), .ra(multiplexer_2_out), .WR(WR_v), .WA(multiplexer_2_out), .rb(v_rb),
    .R(reset), .da(br_pe0_1_da), .db(br_pe0_1_db));
  BR_pe1 br_pe1_1 (
    .CLK(CLK), .WD(multiplexer_13_out), .ra(multiplexer_3_out), .WR(WR_v), .WA(multiplexer_3_out), .rb(v_rb),
    .R(reset), .da(br_pe1_1_da), .db(br_pe1_1_db));
  BR_pe2 br_pe2_1 (
    .CLK(CLK), .WD(multiplexer_14_out), .ra(multiplexer_4_out), .WR(WR_v), .WA(multiplexer_4_out), .rb(v_rb),
    .R(reset), .da(br_pe2_1_da), .db(br_pe2_1_db));
  BR_pe3 br_pe3_1 (
    .CLK(CLK), .WD(multiplexer_15_out), .ra(multiplexer_5_out), .WR(WR_v), .WA(multiplexer_5_out), .rb(v_rb),
    .R(reset), .da(br_pe3_1_da), .db(br_pe3_1_db));
  UC uc_2 (
    .OPCODE(separa_1_e_op), .comp(ula_5_comp), .WM(WM), .pc_s(PcSource), .RS(RS), .r1(r1), .CI(CI), .WR(WR),
    .ula_ctrl(ula_ctrl));
  Multiplexer #(.width(8)) multiplexer_7 (.in0(br_pe0_1_db), .in1(v_imm), .out(multiplexer_7_out), .sel(CI_v));
  // Probe on br_pe0_1_da
  Multiplexer #(.width(8)) multiplexer_8 (.in0(br_pe1_1_db), .in1(v_imm), .out(multiplexer_8_out), .sel(CI_v));
  Multiplexer #(.width(8)) multiplexer_9 (.in0(br_pe2_1_db), .in1(v_imm), .out(multiplexer_9_out), .sel(CI_v));
  BD bd_1 (
    .CLK(CLK), .WD(multiplexer_16_out), .ra(multiplexer_6_out), .WR(WR), .WA(multiplexer_6_out),
    .rb(separa_1_e_rb), .R(reset), .da(bd_1_da), .db(db));
  // Probe on br_pe1_1_da
  // Probe on br_pe2_1_da
  Multiplexer #(.width(8)) multiplexer_10 (.in0(br_pe3_1_db), .in1(v_imm), .out(multiplexer_10_out), .sel(CI_v));
  // Probe on br_pe3_1_da
  Multiplexer #(.width(8)) multiplexer_11 (.in0(db), .in1(e_imm), .out(multiplexer_11_out), .sel(CI));
  // Probe on bd_1_da
  ULA ula_1 (.ula_ctrl(ula_ctrl_v), .op1(br_pe0_1_da), .op2(multiplexer_7_out), .ula_out(ula_out_p0));  // open: comp
  // Probe on br_pe0_1_db
  ULA ula_2 (.ula_ctrl(ula_ctrl_v), .op1(br_pe1_1_da), .op2(multiplexer_8_out), .ula_out(ula_out_p1));  // open: comp
  // Probe on br_pe1_1_db
  ULA ula_3 (.ula_ctrl(ula_ctrl_v), .op1(br_pe2_1_da), .op2(multiplexer_9_out), .ula_out(ula_out_p2));  // open: comp
  ULA ula_4 (.ula_ctrl(ula_ctrl_v), .op1(br_pe3_1_da), .op2(multiplexer_10_out), .ula_out(ula_out_p3));  // open: comp
  RAM #(.enables("line")) ram_1 (.addr(br_pe0_1_db), .we(WM_v), .clk(CLK), .din(br_pe0_1_da), .dout(ram_1_dout));
  RAM #(.enables("line")) ram_2 (.addr(br_pe1_1_db), .we(WM_v), .clk(CLK), .din(br_pe1_1_da), .dout(ram_2_dout));
  // Probe on br_pe2_1_db
  RAM #(.enables("line")) ram_3 (.addr(br_pe2_1_db), .we(WM_v), .clk(CLK), .din(br_pe2_1_da), .dout(ram_3_dout));
  // Probe on br_pe3_1_db
  RAM #(.enables("line")) ram_4 (.addr(br_pe3_1_db), .we(WM_v), .clk(CLK), .din(br_pe3_1_da), .dout(ram_4_dout));
  ULA ula_5 (.ula_ctrl(ula_ctrl), .op1(bd_1_da), .op2(multiplexer_11_out), .ula_out(ula_out), .comp(ula_5_comp));
  // Probe on db
  Multiplexer #(.width(8)) multiplexer_12 (.in0(ula_out_p0), .in1(ram_1_dout), .out(multiplexer_12_out), .sel(RS_v));
  // Probe on RS_v
  Multiplexer #(.width(8)) multiplexer_13 (.in0(ula_out_p1), .in1(ram_2_dout), .out(multiplexer_13_out), .sel(RS_v));
  // Probe on RS_v
  Multiplexer #(.width(8)) multiplexer_14 (.in0(ula_out_p2), .in1(ram_3_dout), .out(multiplexer_14_out), .sel(RS_v));
  // Probe on RS_v
  Multiplexer #(.width(8)) multiplexer_15 (.in0(ula_out_p3), .in1(ram_4_dout), .out(multiplexer_15_out), .sel(RS_v));
  // Probe on RS_v
  RAM #(.enables("line")) ram_5 (.addr(db), .we(WM), .clk(CLK), .din(bd_1_da), .dout(ram_5_dout));
  // Probe on ram_1_dout
  // Probe on ram_2_dout
  // Probe on ram_3_dout
  Multiplexer #(.width(8)) multiplexer_16 (.in0(ula_out), .in1(ram_5_dout), .out(multiplexer_16_out), .sel(RS));
  // Probe on RS
  // Probe on ram_4_dout
  // Probe on ram_5_dout

  // Notes on the sheet:
  //   contents of rom_1 (hex, n*v repeats v):
  //   20 32 49 90 a0 b4 21 37 79 c4 95 20 31 59 d4 df cd a0 b4 c7 20 36 71 20 33 49 a0 bc da c9 df a1 b4
  //   cd 23 34 79 cc c8 9e a0 b4 dc cd d8 c9 20 31 59 22 32 71 20 33 49 a1 b8 da c9 df 24 3b 79 c8 9e a0
  //   b4 d8 c9 20 31 59 23 3c 71 20 33 49 a1 b8 da c8 26 39 79 8e a0 bc c9 86 cd a0 bc c9 9e d9 a0 b8 d9
  //   20 31 59 25 32 71
  //   PE 0
  //   PE 1
  //   PE 2
  //   PE 3
endmodule

module separa (
  input  [7:0] instr,
  output [3:0] v_op,
  output [3:0] e_op,
  output [1:0] v_ra,
  output [1:0] e_ra,
  output [1:0] v_rb,
  output [1:0] e_rb,
  output [7:0] v_imm,
  output [7:0] e_imm
);

  wire not_1_out, not_2_out, not_3_out, not_4_out;
  wire [7:0] imm;

  Multiplexer #(.width(4)) multiplexer_1 (.in0(instr[7:4]), .in1(4'b1100), .out(v_op), .sel(not_1_out));
  not not_1 (not_1_out, instr[7]);
  Multiplexer #(.width(4)) multiplexer_2 (.in0(instr[7:4]), .in1(4'b0100), .out(e_op), .sel(instr[7]));
  Multiplexer #(.width(2)) multiplexer_3 (.in0(instr[3:2]), .in1(2'b00), .out(v_ra), .sel(not_2_out));
  not not_2 (not_2_out, instr[7]);
  Multiplexer #(.width(2)) multiplexer_4 (.in0(instr[3:2]), .in1(2'b00), .out(e_ra), .sel(instr[7]));
  Multiplexer #(.width(2)) multiplexer_5 (.in0(instr[1:0]), .in1(2'b00), .out(v_rb), .sel(not_3_out));
  not not_3 (not_3_out, instr[7]);
  Multiplexer #(.width(2)) multiplexer_6 (.in0(instr[1:0]), .in1(2'b00), .out(e_rb), .sel(instr[7]));
  Multiplexer #(.width(8)) multiplexer_7 (.in0(imm), .in1({8{1'b0}}), .out(v_imm), .sel(not_4_out));
  not not_4 (not_4_out, instr[7]);
  Multiplexer #(.width(8)) multiplexer_8 (.in0(imm), .in1({8{1'b0}}), .out(e_imm), .sel(instr[7]));
  assign imm = {{4{instr[3]}}, instr[3:0]};  // Bit_Extender bit_extender_1

  // Other names for the same wires on the sheet: rb[1:0] = instr[1:0]; ra[1:0] = instr[3:2]; opcode[3:0] = instr[7:4];
  //   eh_vet = instr[7]

  // Notes on the sheet:
  //   rb
endmodule

module BD (
  input  CLK,
  input  [7:0] WD,
  input  [1:0] ra,
  input  WR,
  input  [1:0] WA,
  input  [1:0] rb,
  input  R,
  output [7:0] da,
  output [7:0] db
);

  wire demultiplexer_1_out0, demultiplexer_1_out1, demultiplexer_1_out2, demultiplexer_1_out3;
  wire [7:0] register_1_q, register_2_q, register_3_q, register_4_q;

  Demultiplexer #(.select(2)) demultiplexer_1 (
    .out0(demultiplexer_1_out0), .out1(demultiplexer_1_out1), .out2(demultiplexer_1_out2),
    .out3(demultiplexer_1_out3), .in(WR), .sel(WA));
  Register register_1 (.D({8{1'b0}}), .en(demultiplexer_1_out0), .clk(CLK), .Q(register_1_q), .clr(R));
  Register register_2 (.D(WD), .en(demultiplexer_1_out1), .clk(CLK), .Q(register_2_q), .clr(R));
  Register register_3 (.D(WD), .en(demultiplexer_1_out2), .clk(CLK), .Q(register_3_q), .clr(R));
  Register register_4 (.D(WD), .en(demultiplexer_1_out3), .clk(CLK), .Q(register_4_q), .clr(R));
  Multiplexer #(.select(2), .width(8)) multiplexer_1 (
    .in0(register_1_q), .in1(register_2_q), .in2(register_3_q), .in3(register_4_q), .out(da), .sel(ra));
  Multiplexer #(.select(2), .width(8)) multiplexer_2 (
    .in0(register_1_q), .in1(register_2_q), .in2(register_3_q), .in3(register_4_q), .out(db), .sel(rb));
endmodule

module ULA (
  input  [2:0] ula_ctrl,
  input  [7:0] op1,
  input  [7:0] op2,
  output [7:0] ula_out,
  output comp
);

  wire [7:0] adder_1_out, and_1_out, bit_extender_1_out, or_1_out, subtractor_1_out;

  assign or_1_out = op1 | op2;  // OR_Gate or_1, 8 bits wide
  Adder adder_1 (.a(op1), .b(op2), .out(adder_1_out));  // open: cin, cout
  Subtractor subtractor_1 (.a(op1), .b(op2), .out(subtractor_1_out));  // open: bin, bout
  assign and_1_out = op1 & op2;  // AND_Gate and_1, 8 bits wide
  Comparator comparator_1 (.a(op1), .b({8{1'b0}}), .eq(comp));  // open: gt, lt
  assign bit_extender_1_out = {{7{comp}}, comp};  // Bit_Extender bit_extender_1
  Multiplexer #(.select(3), .width(8)) multiplexer_1 (
    .in1(or_1_out), .in2({op2[3:0], op1[3:0]}), .in3({op1[7:4], op2[3:0]}), .in4(adder_1_out),
    .in5(subtractor_1_out), .in6(and_1_out), .in7(bit_extender_1_out), .out(ula_out), .sel(ula_ctrl));  // open: in0

  // Notes on the sheet:
  //   movh
  //   movL
endmodule

module UC (
  input  [3:0] OPCODE,
  input  comp,
  output WM,
  output pc_s,
  output RS,
  output r1,
  output CI,
  output WR,
  output [2:0] ula_ctrl
);

  wire and_2_out, and_5_out, and_6_out, and_7_out, and_8_out, and_9_out, and_10_out, and_11_out, not_1_out,
       not_2_out, not_3_out, not_4_out, not_5_out, not_6_out, not_8_out, not_9_out, not_10_out, not_11_out,
       not_12_out, not_13_out, not_14_out, not_15_out, not_16_out;

  not not_1 (not_1_out, OPCODE[2]);
  not not_2 (not_2_out, OPCODE[1]);
  not not_3 (not_3_out, OPCODE[3]);
  not not_4 (not_4_out, OPCODE[2]);
  not not_5 (not_5_out, OPCODE[1]);
  not not_6 (not_6_out, OPCODE[2]);
  not not_7 (CI, OPCODE[2]);
  not not_8 (not_8_out, OPCODE[2]);
  not not_9 (not_9_out, OPCODE[1]);
  not not_10 (not_10_out, OPCODE[0]);
  not not_11 (not_11_out, OPCODE[3]);
  not not_12 (not_12_out, OPCODE[0]);
  not not_13 (not_13_out, OPCODE[1]);
  not not_14 (not_14_out, OPCODE[3]);
  not not_15 (not_15_out, OPCODE[2]);
  not not_16 (not_16_out, OPCODE[0]);
  and and_1 (WM, not_1_out, not_2_out, OPCODE[0]);
  and and_2 (and_2_out, OPCODE[2], OPCODE[1], OPCODE[0], not_3_out);
  and and_3 (RS, not_4_out, not_5_out);
  and and_4 (r1, OPCODE[1], not_6_out);
  and and_5 (and_5_out, OPCODE[3], OPCODE[1]);
  and and_6 (and_6_out, not_8_out, OPCODE[1]);
  and and_7 (and_7_out, OPCODE[2], not_9_out);
  and and_8 (and_8_out, not_11_out, OPCODE[2]);
  and and_9 (and_9_out, OPCODE[2], not_12_out);
  and and_10 (and_10_out, not_14_out, OPCODE[1]);
  and and_11 (and_11_out, OPCODE[1], not_16_out);
  and and_12 (pc_s, and_2_out, comp);
  or or_1 (WR, and_5_out, and_6_out, and_7_out, not_10_out);
  or or_2 (ula_ctrl[2], and_8_out, and_9_out, not_13_out);
  or or_3 (ula_ctrl[1], and_10_out, not_15_out, and_11_out);

  assign ula_ctrl[0] = OPCODE[0];

  // Other names for the same wires on the sheet: op1 = OPCODE[1]; op2 = OPCODE[2]; op3 = OPCODE[3]; op0 = OPCODE[0]
endmodule

module BR_pe0 (
  input  CLK,
  input  [7:0] WD,
  input  [1:0] ra,
  input  WR,
  input  [1:0] WA,
  input  [1:0] rb,
  input  R,
  output [7:0] da,
  output [7:0] db
);

  wire demultiplexer_1_out0, demultiplexer_1_out1, demultiplexer_1_out2, demultiplexer_1_out3;
  wire [7:0] register_1_q, register_2_q, register_3_q, register_4_q;

  Demultiplexer #(.select(2)) demultiplexer_1 (
    .out0(demultiplexer_1_out0), .out1(demultiplexer_1_out1), .out2(demultiplexer_1_out2),
    .out3(demultiplexer_1_out3), .in(WR), .sel(WA));
  Register register_1 (.D({8{1'b0}}), .en(demultiplexer_1_out0), .clk(CLK), .Q(register_1_q), .clr(R));
  Register register_2 (.D(WD), .en(demultiplexer_1_out1), .clk(CLK), .Q(register_2_q), .clr(R));
  Register register_3 (.D(WD), .en(demultiplexer_1_out2), .clk(CLK), .Q(register_3_q), .clr(R));
  Register register_4 (.D(WD), .en(demultiplexer_1_out3), .clk(CLK), .Q(register_4_q), .clr(R));
  Multiplexer #(.select(2), .width(8)) multiplexer_1 (
    .in0(register_1_q), .in1(register_2_q), .in2(register_3_q), .in3(register_4_q), .out(da), .sel(ra));
  Multiplexer #(.select(2), .width(8)) multiplexer_2 (
    .in0(register_1_q), .in1(register_2_q), .in2(register_3_q), .in3(register_4_q), .out(db), .sel(rb));
endmodule

module BR_pe1 (
  input  CLK,
  input  [7:0] WD,
  input  [1:0] ra,
  input  WR,
  input  [1:0] WA,
  input  [1:0] rb,
  input  R,
  output [7:0] da,
  output [7:0] db
);

  wire demultiplexer_1_out0, demultiplexer_1_out1, demultiplexer_1_out2, demultiplexer_1_out3;
  wire [7:0] register_1_q, register_2_q, register_3_q, register_4_q;

  Demultiplexer #(.select(2)) demultiplexer_1 (
    .out0(demultiplexer_1_out0), .out1(demultiplexer_1_out1), .out2(demultiplexer_1_out2),
    .out3(demultiplexer_1_out3), .in(WR), .sel(WA));
  Register register_1 (.D(8'h1), .en(demultiplexer_1_out0), .clk(CLK), .Q(register_1_q), .clr(R));
  Register register_2 (.D(WD), .en(demultiplexer_1_out1), .clk(CLK), .Q(register_2_q), .clr(R));
  Register register_3 (.D(WD), .en(demultiplexer_1_out2), .clk(CLK), .Q(register_3_q), .clr(R));
  Register register_4 (.D(WD), .en(demultiplexer_1_out3), .clk(CLK), .Q(register_4_q), .clr(R));
  Multiplexer #(.select(2), .width(8)) multiplexer_1 (
    .in0(register_1_q), .in1(register_2_q), .in2(register_3_q), .in3(register_4_q), .out(da), .sel(ra));
  Multiplexer #(.select(2), .width(8)) multiplexer_2 (
    .in0(register_1_q), .in1(register_2_q), .in2(register_3_q), .in3(register_4_q), .out(db), .sel(rb));
endmodule

module BR_pe2 (
  input  CLK,
  input  [7:0] WD,
  input  [1:0] ra,
  input  WR,
  input  [1:0] WA,
  input  [1:0] rb,
  input  R,
  output [7:0] da,
  output [7:0] db
);

  wire demultiplexer_1_out0, demultiplexer_1_out1, demultiplexer_1_out2, demultiplexer_1_out3;
  wire [7:0] register_1_q, register_2_q, register_3_q, register_4_q;

  Demultiplexer #(.select(2)) demultiplexer_1 (
    .out0(demultiplexer_1_out0), .out1(demultiplexer_1_out1), .out2(demultiplexer_1_out2),
    .out3(demultiplexer_1_out3), .in(WR), .sel(WA));
  Register register_1 (.D(8'h2), .en(demultiplexer_1_out0), .clk(CLK), .Q(register_1_q), .clr(R));
  Register register_2 (.D(WD), .en(demultiplexer_1_out1), .clk(CLK), .Q(register_2_q), .clr(R));
  Register register_3 (.D(WD), .en(demultiplexer_1_out2), .clk(CLK), .Q(register_3_q), .clr(R));
  Register register_4 (.D(WD), .en(demultiplexer_1_out3), .clk(CLK), .Q(register_4_q), .clr(R));
  Multiplexer #(.select(2), .width(8)) multiplexer_1 (
    .in0(register_1_q), .in1(register_2_q), .in2(register_3_q), .in3(register_4_q), .out(da), .sel(ra));
  Multiplexer #(.select(2), .width(8)) multiplexer_2 (
    .in0(register_1_q), .in1(register_2_q), .in2(register_3_q), .in3(register_4_q), .out(db), .sel(rb));
endmodule

module BR_pe3 (
  input  CLK,
  input  [7:0] WD,
  input  [1:0] ra,
  input  WR,
  input  [1:0] WA,
  input  [1:0] rb,
  input  R,
  output [7:0] da,
  output [7:0] db
);

  wire demultiplexer_1_out0, demultiplexer_1_out1, demultiplexer_1_out2, demultiplexer_1_out3;
  wire [7:0] register_1_q, register_2_q, register_3_q, register_4_q;

  Demultiplexer #(.select(2)) demultiplexer_1 (
    .out0(demultiplexer_1_out0), .out1(demultiplexer_1_out1), .out2(demultiplexer_1_out2),
    .out3(demultiplexer_1_out3), .in(WR), .sel(WA));
  Register register_1 (.D(8'h3), .en(demultiplexer_1_out0), .clk(CLK), .Q(register_1_q), .clr(R));
  Register register_2 (.D(WD), .en(demultiplexer_1_out1), .clk(CLK), .Q(register_2_q), .clr(R));
  Register register_3 (.D(WD), .en(demultiplexer_1_out2), .clk(CLK), .Q(register_3_q), .clr(R));
  Register register_4 (.D(WD), .en(demultiplexer_1_out3), .clk(CLK), .Q(register_4_q), .clr(R));
  Multiplexer #(.select(2), .width(8)) multiplexer_1 (
    .in0(register_1_q), .in1(register_2_q), .in2(register_3_q), .in3(register_4_q), .out(da), .sel(ra));
  Multiplexer #(.select(2), .width(8)) multiplexer_2 (
    .in0(register_1_q), .in1(register_2_q), .in2(register_3_q), .in3(register_4_q), .out(db), .sel(rb));
endmodule
